// Logisim project tennis — копия.circ as structural Verilog: 9 circuits, main circuit main
module main (
);

  wire AGAIN_out;
  wire [3:0] binaryto3dig_1_hundreds, binaryto3dig_1_ones, binaryto3dig_1_tens, binaryto3dig_2_hundreds,
       binaryto3dig_2_ones, binaryto3dig_2_tens;
  wire [4:0] correctjoystik_1_joystikout, joystick_1_y, kinematiccontrollerbase_1_ballxout,
       kinematiccontrollerbase_1_ballyout, kinematiccontrollerbase_1_chip_id, videosection_1_outballx,
       videosection_1_outbally, videosection_1_outchipid, videosection_1_outleftbary,
       videosection_1_outrightbary, videosection_2_outballx, videosection_2_outbally,
       videosection_2_outchipid, videosection_2_outleftbary, videosection_2_outrightbary,
       videosection_3_outballx, videosection_3_outbally, videosection_3_outchipid,
       videosection_3_outleftbary, videosection_3_outrightbary;
  wire [7:0] kinematiccontrollerbase_1_scoreleft, kinematiccontrollerbase_1_scoreright;
  wire [31:0] videosection_1_col0, videosection_1_col1, videosection_1_col2, videosection_1_col3,
       videosection_1_col4, videosection_1_col5, videosection_1_col6, videosection_1_col7,
       videosection_2_col0, videosection_2_col1, videosection_2_col2, videosection_2_col3,
       videosection_2_col4, videosection_2_col5, videosection_2_col6, videosection_2_col7,
       videosection_3_col0, videosection_3_col1, videosection_3_col2, videosection_3_col3,
       videosection_3_col4, videosection_3_col5, videosection_3_col6, videosection_3_col7,
       videosection_4_col0, videosection_4_col1, videosection_4_col2, videosection_4_col3,
       videosection_4_col4, videosection_4_col5, videosection_4_col6, videosection_4_col7;

  Hex_Digit_Display hex_digit_display_1 (.value(binaryto3dig_1_hundreds));  // open: dp
  Hex_Digit_Display hex_digit_display_2 (.value(binaryto3dig_1_tens));  // open: dp
  Button AGAIN (.out(AGAIN_out));
  Joystick #(.bits(5)) joystick_1 (.y(joystick_1_y));  // open: x
  CorrectJoystik correctjoystik_1 (.Joystik(joystick_1_y), .JoystikOut(correctjoystik_1_joystikout));
  Hex_Digit_Display hex_digit_display_3 (.value(binaryto3dig_1_ones));  // open: dp
  Binaryto3Dig binaryto3dig_1 (
    .number(kinematiccontrollerbase_1_scoreleft), .hundreds(binaryto3dig_1_hundreds),
    .tens(binaryto3dig_1_tens), .ones(binaryto3dig_1_ones));
  DotMatrix #(.matrixcols(32), .matrixrows(32)) dotmatrix_1 (
    .col0(videosection_1_col0), .col1(videosection_1_col1), .col2(videosection_1_col2),
    .col3(videosection_1_col3), .col4(videosection_1_col4), .col5(videosection_1_col5),
    .col6(videosection_1_col6), .col7(videosection_1_col7), .col8(videosection_2_col0),
    .col9(videosection_2_col1), .col10(videosection_2_col2), .col11(videosection_2_col3),
    .col12(videosection_2_col4), .col13(videosection_2_col5), .col14(videosection_2_col6),
    .col15(videosection_2_col7), .col16(videosection_3_col0), .col17(videosection_3_col1),
    .col18(videosection_3_col2), .col19(videosection_3_col3), .col20(videosection_3_col4),
    .col21(videosection_3_col5), .col22(videosection_3_col6), .col23(videosection_3_col7),
    .col24(videosection_4_col0), .col25(videosection_4_col1), .col26(videosection_4_col2),
    .col27(videosection_4_col3), .col28(videosection_4_col4), .col29(videosection_4_col5),
    .col30(videosection_4_col6), .col31(videosection_4_col7));
  VideoSection videosection_1 (
    .BallX(kinematiccontrollerbase_1_ballxout), .BallY(kinematiccontrollerbase_1_ballyout),
    .LeftbarY(correctjoystik_1_joystikout), .RightbarY({5{1'b0}}), .col1(videosection_1_col1),
    .col3(videosection_1_col3), .col5(videosection_1_col5), .col7(videosection_1_col7),
    .col0(videosection_1_col0), .col2(videosection_1_col2), .col4(videosection_1_col4),
    .col6(videosection_1_col6), .OutBallX(videosection_1_outballx), .OutBallY(videosection_1_outbally),
    .OutLeftbarY(videosection_1_outleftbary), .OutRightbarY(videosection_1_outrightbary),
    .ChipID(kinematiccontrollerbase_1_chip_id), .OutChipID(videosection_1_outchipid));
  KinematicControllerBase kinematiccontrollerbase_1 (
    .Reset(AGAIN_out), .LeftbarY(correctjoystik_1_joystikout), .RightbarY({5{1'b0}}),
    .ScoreLeft(kinematiccontrollerbase_1_scoreleft), .ScoreRight(kinematiccontrollerbase_1_scoreright),
    .BallXout(kinematiccontrollerbase_1_ballxout), .BallYout(kinematiccontrollerbase_1_ballyout),
    .Chip_ID(kinematiccontrollerbase_1_chip_id));
  VideoSection videosection_2 (
    .BallX(videosection_1_outballx), .BallY(videosection_1_outbally), .LeftbarY(videosection_1_outleftbary),
    .RightbarY(videosection_1_outrightbary), .col1(videosection_2_col1), .col3(videosection_2_col3),
    .col5(videosection_2_col5), .col7(videosection_2_col7), .col0(videosection_2_col0),
    .col2(videosection_2_col2), .col4(videosection_2_col4), .col6(videosection_2_col6),
    .OutBallX(videosection_2_outballx), .OutBallY(videosection_2_outbally),
    .OutLeftbarY(videosection_2_outleftbary), .OutRightbarY(videosection_2_outrightbary),
    .ChipID(videosection_1_outchipid), .OutChipID(videosection_2_outchipid));
  VideoSection videosection_3 (
    .BallX(videosection_2_outballx), .BallY(videosection_2_outbally), .LeftbarY(videosection_2_outleftbary),
    .RightbarY(videosection_2_outrightbary), .col1(videosection_3_col1), .col3(videosection_3_col3),
    .col5(videosection_3_col5), .col7(videosection_3_col7), .col0(videosection_3_col0),
    .col2(videosection_3_col2), .col4(videosection_3_col4), .col6(videosection_3_col6),
    .OutBallX(videosection_3_outballx), .OutBallY(videosection_3_outbally),
    .OutLeftbarY(videosection_3_outleftbary), .OutRightbarY(videosection_3_outrightbary),
    .ChipID(videosection_2_outchipid), .OutChipID(videosection_3_outchipid));
  VideoSection videosection_4 (
    .BallX(videosection_3_outballx), .BallY(videosection_3_outbally), .LeftbarY(videosection_3_outleftbary),
    .RightbarY(videosection_3_outrightbary), .col1(videosection_4_col1), .col3(videosection_4_col3),
    .col5(videosection_4_col5), .col7(videosection_4_col7), .col0(videosection_4_col0),
    .col2(videosection_4_col2), .col4(videosection_4_col4), .col6(videosection_4_col6),
    .ChipID(videosection_3_outchipid));  // open: OutBallX, OutBallY, OutLeftbarY, OutRightbarY, OutChipID
  Hex_Digit_Display hex_digit_display_4 (.value(binaryto3dig_2_hundreds));  // open: dp
  Hex_Digit_Display hex_digit_display_5 (.value(binaryto3dig_2_tens));  // open: dp
  Hex_Digit_Display hex_digit_display_6 (.value(binaryto3dig_2_ones));  // open: dp
  Binaryto3Dig binaryto3dig_2 (
    .number(kinematiccontrollerbase_1_scoreright), .hundreds(binaryto3dig_2_hundreds),
    .tens(binaryto3dig_2_tens), .ones(binaryto3dig_2_ones));
endmodule

module VideoChip (
  input  [4:0] ChipID,
  input  [4:0] BallX,
  input  [4:0] BallY,
  input  [4:0] LeftbarY,
  input  [4:0] RightbarY,
  output [4:0] OutChipID,
  output [4:0] OutBallX,
  output [4:0] OutBallY,
  output [4:0] OutLeftbarY,
  output [4:0] OutRightbarY,
  output [31:0] Display
);

  wire ball, left, right;
  wire [31:0] and_1_out, and_2_out, and_3_out, bit_extender_1_out, bit_extender_2_out, bit_extender_3_out,
       shifter_1_out, shifter_2_out, shifter_3_out;

  Adder #(.width(5)) adder_1 (.a(ChipID), .b(5'b00001), .out(OutChipID));  // open: cin, cout
  Comparator #(.width(5)) comparator_1 (.a(ChipID), .b(BallX), .eq(ball));  // open: gt, lt
  // Probe on 32'h7
  assign bit_extender_1_out = {{31{left}}, left};  // Bit_Extender bit_extender_1
  assign bit_extender_2_out = {{31{right}}, right};  // Bit_Extender bit_extender_2
  assign bit_extender_3_out = {{31{ball}}, ball};  // Bit_Extender bit_extender_3
  Shifter #(.width(32)) shifter_1 (.in(32'h7), .\dist (LeftbarY), .out(shifter_1_out));
  Shifter #(.width(32)) shifter_2 (.in(32'h7), .\dist (RightbarY), .out(shifter_2_out));
  Shifter #(.width(32)) shifter_3 (.in(32'h1), .\dist (BallY), .out(shifter_3_out));
  assign and_1_out = shifter_1_out & bit_extender_1_out;  // AND_Gate and_1, 32 bits wide
  assign Display = and_1_out | and_2_out | and_3_out;  // OR_Gate or_1, 32 bits wide
  assign and_2_out = shifter_2_out & bit_extender_2_out;  // AND_Gate and_2, 32 bits wide
  assign and_3_out = shifter_3_out & bit_extender_3_out;  // AND_Gate and_3, 32 bits wide
  Comparator #(.width(5)) comparator_2 (.a(ChipID), .b(5'b00011), .eq(left));  // open: gt, lt
  // Probe on 5'b00011
  Comparator #(.width(5)) comparator_3 (.a(ChipID), .b(5'b11100), .eq(right));  // open: gt, lt
  // Probe on 5'b11100

  assign OutBallX = BallX;
  assign OutBallY = BallY;
  assign OutLeftbarY = LeftbarY;
  assign OutRightbarY = RightbarY;

  // Notes on the sheet:
  //   Ball Column?
  //   3 column?
  //   28 column?
endmodule

module VideoSection (
  input  [4:0] ChipID,
  input  [4:0] BallX,
  input  [4:0] BallY,
  input  [4:0] LeftbarY,
  input  [4:0] RightbarY,
  output [31:0] col1,
  output [31:0] col3,
  output [31:0] col5,
  output [31:0] col7,
  output [4:0] OutChipID,
  output [4:0] OutBallX,
  output [4:0] OutBallY,
  output [4:0] OutLeftbarY,
  output [4:0] OutRightbarY,
  output [31:0] col0,
  output [31:0] col2,
  output [31:0] col4,
  output [31:0] col6
);

  wire [4:0] videochip_1_outballx, videochip_1_outbally, videochip_1_outchipid, videochip_1_outleftbary,
       videochip_1_outrightbary, videochip_2_outballx, videochip_2_outbally, videochip_2_outchipid,
       videochip_2_outleftbary, videochip_2_outrightbary, videochip_3_outballx, videochip_3_outbally,
       videochip_3_outchipid, videochip_3_outleftbary, videochip_3_outrightbary, videochip_4_outballx,
       videochip_4_outbally, videochip_4_outchipid, videochip_4_outleftbary, videochip_4_outrightbary,
       videochip_5_outballx, videochip_5_outbally, videochip_5_outchipid, videochip_5_outleftbary,
       videochip_5_outrightbary, videochip_6_outballx, videochip_6_outbally, videochip_6_outchipid,
       videochip_6_outleftbary, videochip_6_outrightbary, videochip_7_outballx, videochip_7_outbally,
       videochip_7_outchipid, videochip_7_outleftbary, videochip_7_outrightbary;

  VideoChip videochip_1 (
    .ChipID(videochip_2_outchipid), .BallX(videochip_2_outballx), .BallY(videochip_2_outbally),
    .LeftbarY(videochip_2_outleftbary), .RightbarY(videochip_2_outrightbary),
    .OutChipID(videochip_1_outchipid), .OutBallX(videochip_1_outballx), .OutBallY(videochip_1_outbally),
    .OutLeftbarY(videochip_1_outleftbary), .OutRightbarY(videochip_1_outrightbary), .Display(col1));
  VideoChip videochip_2 (
    .ChipID(ChipID), .BallX(BallX), .BallY(BallY), .LeftbarY(LeftbarY), .RightbarY(RightbarY),
    .OutChipID(videochip_2_outchipid), .OutBallX(videochip_2_outballx), .OutBallY(videochip_2_outbally),
    .OutLeftbarY(videochip_2_outleftbary), .OutRightbarY(videochip_2_outrightbary), .Display(col0));
  VideoChip videochip_3 (
    .ChipID(videochip_1_outchipid), .BallX(videochip_1_outballx), .BallY(videochip_1_outbally),
    .LeftbarY(videochip_1_outleftbary), .RightbarY(videochip_1_outrightbary),
    .OutChipID(videochip_3_outchipid), .OutBallX(videochip_3_outballx), .OutBallY(videochip_3_outbally),
    .OutLeftbarY(videochip_3_outleftbary), .OutRightbarY(videochip_3_outrightbary), .Display(col2));
  VideoChip videochip_4 (
    .ChipID(videochip_3_outchipid), .BallX(videochip_3_outballx), .BallY(videochip_3_outbally),
    .LeftbarY(videochip_3_outleftbary), .RightbarY(videochip_3_outrightbary),
    .OutChipID(videochip_4_outchipid), .OutBallX(videochip_4_outballx), .OutBallY(videochip_4_outbally),
    .OutLeftbarY(videochip_4_outleftbary), .OutRightbarY(videochip_4_outrightbary), .Display(col3));
  VideoChip videochip_5 (
    .ChipID(videochip_4_outchipid), .BallX(videochip_4_outballx), .BallY(videochip_4_outbally),
    .LeftbarY(videochip_4_outleftbary), .RightbarY(videochip_4_outrightbary),
    .OutChipID(videochip_5_outchipid), .OutBallX(videochip_5_outballx), .OutBallY(videochip_5_outbally),
    .OutLeftbarY(videochip_5_outleftbary), .OutRightbarY(videochip_5_outrightbary), .Display(col4));
  VideoChip videochip_6 (
    .ChipID(videochip_5_outchipid), .BallX(videochip_5_outballx), .BallY(videochip_5_outbally),
    .LeftbarY(videochip_5_outleftbary), .RightbarY(videochip_5_outrightbary),
    .OutChipID(videochip_6_outchipid), .OutBallX(videochip_6_outballx), .OutBallY(videochip_6_outbally),
    .OutLeftbarY(videochip_6_outleftbary), .OutRightbarY(videochip_6_outrightbary), .Display(col5));
  VideoChip videochip_7 (
    .ChipID(videochip_6_outchipid), .BallX(videochip_6_outballx), .BallY(videochip_6_outbally),
    .LeftbarY(videochip_6_outleftbary), .RightbarY(videochip_6_outrightbary),
    .OutChipID(videochip_7_outchipid), .OutBallX(videochip_7_outballx), .OutBallY(videochip_7_outbally),
    .OutLeftbarY(videochip_7_outleftbary), .OutRightbarY(videochip_7_outrightbary), .Display(col6));
  VideoChip videochip_8 (
    .ChipID(videochip_7_outchipid), .BallX(videochip_7_outballx), .BallY(videochip_7_outbally),
    .LeftbarY(videochip_7_outleftbary), .RightbarY(videochip_7_outrightbary), .OutChipID(OutChipID),
    .OutBallX(OutBallX), .OutBallY(OutBallY), .OutLeftbarY(OutLeftbarY), .OutRightbarY(OutRightbarY),
    .Display(col7));
endmodule

module Reflect (
  input  [2:0] oldv,
  output [2:0] newv
);

  wire comparator_1_eq;
  wire [2:0] negator_1_out, not_1_out;

  Negator #(.width(3)) negator_1 (.in(oldv), .out(negator_1_out));
  assign not_1_out = ~oldv;  // NOT_Gate not_1, 3 bits wide
  Comparator #(.width(3)) comparator_1 (.a(oldv), .b(3'b100), .eq(comparator_1_eq));  // open: gt, lt
  Multiplexer #(.width(3)) multiplexer_1 (
    .in0(negator_1_out), .in1(not_1_out), .out(newv), .sel(comparator_1_eq));  // open: en

  // Notes on the sheet:
  //   Измнение направления движения мяча
  //   -(-4) = 3
endmodule

module Inrange (
  input  [4:0] Yball,
  input  [4:0] Ybat,
  output shareArrow
);

  wire comparator_1_eq, comparator_2_eq, comparator_3_eq;
  wire [4:0] adder_1_out, adder_2_out;

  Adder #(.width(5)) adder_1 (.a(Ybat), .b(5'b00001), .out(adder_1_out));  // open: cin, cout
  Adder #(.width(5)) adder_2 (.a(Ybat), .b(5'b00010), .out(adder_2_out));  // open: cin, cout
  Comparator #(.width(5)) comparator_1 (.a(Yball), .b(Ybat), .eq(comparator_1_eq));  // open: gt, lt
  Comparator #(.width(5)) comparator_2 (.a(Yball), .b(adder_1_out), .eq(comparator_2_eq));  // open: gt, lt
  Comparator #(.width(5)) comparator_3 (.a(Yball), .b(adder_2_out), .eq(comparator_3_eq));  // open: gt, lt
  or or_1 (shareArrow, comparator_1_eq, comparator_2_eq, comparator_3_eq);

  // Notes on the sheet:
  //   находится ли мяч в одном из рядов экрана, занятых одной из ракеток
endmodule

module KinematicControllerBase (
  input  Reset,
  input  [4:0] LeftbarY,
  input  [4:0] RightbarY,
  output [4:0] Chip_ID,
  output [7:0] ScoreLeft,
  output [7:0] ScoreRight,
  output [4:0] BallXout,
  output [4:0] BallYout
);

  wire and_1_out, bat, carryX, carryY, Clock, left_wall, or_1_out, or_2_out, right_wall, vx_change, vy_change;
  wire [2:0] multiplexer_3_out, multiplexer_4_out, multiplexer_5_out, multiplexer_6_out, reflect_1_newv,
       reflect_2_newv, vx_reg, vy_reg, Xregout, Yregout;
  wire [7:0] long_vx, long_vy, multiplexer_1_out, multiplexer_2_out, newXreg, newYreg;

  Clock clock_1 (.out(Clock));
  and and_1 (and_1_out, ~vx_change, ~bat);  // AND_Gate
  // Probe on 8'h80
  or or_1 (or_1_out, ~vy_change, Reset);  // OR_Gate
  Counter counter_1 (.count(right_wall), .Q(ScoreLeft), .clk(Clock), .clr(Reset));  // open: load, D, carry
  Counter counter_2 (.count(left_wall), .Q(ScoreRight), .clk(Clock), .clr(Reset));  // open: load, D, carry
  // Probe on 8'hc0
  Multiplexer #(.width(8)) multiplexer_1 (
    .in0(newXreg), .in1(8'hc0), .out(multiplexer_1_out), .sel(Reset));  // open: en
  or or_2 (or_2_out, and_1_out, Reset);
  Multiplexer #(.width(8)) multiplexer_2 (
    .in0(newYreg), .in1(8'h80), .out(multiplexer_2_out), .sel(Reset));  // open: en
  // Probe on {BallXout, Xregout}
  Register #(.trigger("falling")) Xreg (
    .D(multiplexer_1_out), .en(or_2_out), .Q({BallXout, Xregout}), .clk(Clock));  // open: clr
  // Probe on {BallYout, Yregout}
  Register #(.trigger("falling")) Yreg (
    .D(multiplexer_2_out), .en(or_1_out), .Q({BallYout, Yregout}), .clk(Clock));  // open: clr
  // Probe on 3'b110
  Multiplexer #(.width(3)) multiplexer_3 (
    .in0(vx_reg), .in1(reflect_1_newv), .out(multiplexer_3_out), .sel(vx_change));  // open: en
  Reflect reflect_1 (.oldv(vx_reg), .newv(reflect_1_newv));
  // Probe on 3'b001
  Multiplexer #(.width(3)) multiplexer_4 (
    .in0(vy_reg), .in1(reflect_2_newv), .out(multiplexer_4_out), .sel(vy_change));  // open: en
  Reflect reflect_2 (.oldv(vy_reg), .newv(reflect_2_newv));
  Register #(.width(3)) VXreg (.D(multiplexer_5_out), .Q(vx_reg), .clk(Clock));  // open: en, clr
  Multiplexer #(.width(3)) multiplexer_5 (
    .in0(multiplexer_3_out), .in1(3'b110), .out(multiplexer_5_out), .sel(Reset));  // open: en
  Multiplexer #(.width(3)) multiplexer_6 (
    .in0(multiplexer_4_out), .in1(3'b001), .out(multiplexer_6_out), .sel(Reset));  // open: en
  Register #(.width(3)) VYreg (.D(multiplexer_6_out), .Q(vy_reg), .clk(Clock));  // open: en, clr
  assign long_vx = {{5{vx_reg[2]}}, vx_reg};  // Bit_Extender bit_extender_1
  assign long_vy = {{5{vy_reg[2]}}, vy_reg};  // Bit_Extender bit_extender_2
  Adder adder_1 (.a(long_vx), .b({BallXout, Xregout}), .out(newXreg), .cout(carryX));  // open: cin
  Adder adder_2 (.a(long_vy), .b({BallYout, Yregout}), .out(newYreg), .cout(carryY));  // open: cin

  assign Chip_ID = {5{1'b0}};

  // Other names for the same wires on the sheet: BallX[4:0] = BallXout; Xregout[7:3] = BallXout;
  //   BallY[4:0] = BallYout; Yregout[7:3] = BallYout; vx_sign = vx_reg[2]; vy_sign = vy_reg[2]

  // Notes on the sheet:
  //   Координаты мяча
  //   Счетчики
  //   регистры имеют разные триггеры
  //   и не было путаницы
  //   чтобы изменение происходили в разные "фазы"
endmodule

module Process (
);

  wire and_1_out, and_2_out, cdm_8_mark5_1_p1, cdm_8_mark5_1_p2, cdm_8_mark5_1_p3, clock_2_out, clock_3_out,
       comparator_1_eq, comparator_2_eq, mem, not_1_out, read_write, undriven, undriven_2;
  wire [7:0] addr, cdm_8_mark5_1_p7, cdm_8_mark5_1_p8, cdm_8_mark5_1_p9, cdm_8_mark5_1_p10, data;

  // Probe on undriven_2
  // Probe on undriven_2
  // Probe on undriven
  // Probe on undriven
  // Probe on cdm_8_mark5_1_p3
  // Probe on cdm_8_mark5_1_p2
  // CdM_8_mark5 cdm_8_mark5_1: pin names not known; wires that end beside it: cdm_8_mark5_1_p1, cdm_8_mark5_1_p2, cdm_8_mark5_1_p3, mem, read_write, addr, cdm_8_mark5_1_p7, cdm_8_mark5_1_p8, cdm_8_mark5_1_p9, cdm_8_mark5_1_p10, read_write
  Comparator comparator_1 (.a(addr), .b(8'hf3), .eq(comparator_1_eq));  // open: gt, lt
  Comparator comparator_2 (.a(addr), .b(8'hf4), .eq(comparator_2_eq));  // open: gt, lt
  assign data = not_1_out ? cdm_8_mark5_1_p7 : 8'bz;  // Controlled_Buffer controlled_buffer_1
  not not_1 (not_1_out, read_write);
  assign cdm_8_mark5_1_p8 = read_write ? data : 8'bz;  // Controlled_Buffer controlled_buffer_2
  and and_1 (and_1_out, comparator_1_eq, ~read_write, mem);  // AND_Gate
  and and_2 (and_2_out, comparator_2_eq, ~read_write, mem);  // AND_Gate
  Clock clock_1 (.out(cdm_8_mark5_1_p1));
  Register register_1 (.D(data), .en(and_1_out), .Q(cdm_8_mark5_1_p9), .clk(clock_2_out));  // open: clr
  Clock clock_2 (.out(clock_2_out));
  Register register_2 (.D(data), .en(and_2_out), .Q(cdm_8_mark5_1_p10), .clk(clock_3_out));  // open: clr
  Clock clock_3 (.out(clock_3_out));
  RAM ram_1 (.addr(addr), .data(data), .sel(mem), .clk(cdm_8_mark5_1_p1), .ld(read_write));  // open: clr
endmodule

module CorrectJoystik (
  input  [4:0] Joystik,
  output [4:0] JoystikOut
);

  wire comparator_1_gt;
  wire [4:0] subtractor_1_out;

  // Probe on {5{1'b1}}
  Subtractor #(.width(5)) subtractor_1 (.a({5{1'b1}}), .b(Joystik), .out(subtractor_1_out));  // open: bin, bout
  // Probe on 5'b11101
  Multiplexer #(.width(5)) multiplexer_1 (
    .in0(subtractor_1_out), .in1(5'b11101), .out(JoystikOut), .sel(comparator_1_gt));  // open: en
  Comparator #(.width(5), .mode("unsigned")) comparator_1 (
    .a(subtractor_1_out), .b(5'b11101), .gt(comparator_1_gt));  // open: eq, lt
endmodule

module Binaryto3Dig (
  input  [7:0] number,
  output [3:0] hundreds,
  output [3:0] tens,
  output [3:0] ones
);

  wire [7:0] divider_1_out;
  wire [7:4] divider_1_rem, divider_2_out, divider_2_rem;

  // Probe on number
  Divider divider_1 (.a(number), .b(8'ha), .out(divider_1_out), .rem({divider_1_rem, ones}));  // open: upper
  Divider divider_2 (
    .a(divider_1_out), .b(8'ha), .out({divider_2_out, hundreds}), .rem({divider_2_rem, tens}));  // open: upper
  // Probe on ones
  // Probe on hundreds
  // Probe on tens
endmodule
