// Logisim project tennis.circ as structural Verilog: 20 circuits, main circuit main
module main (
);

  wire AGAIN_out, mode, modeout, winleft, winright;
  wire [3:0] binaryto3dig_1_hundreds, binaryto3dig_1_ones, binaryto3dig_1_tens, binaryto3dig_2_hundreds,
       binaryto3dig_2_ones, binaryto3dig_2_tens;
  wire [4:0] joystick_1_y, joystik, kinematiccontrollerbase_1_ballxout, kinematiccontrollerbase_1_ballyout,
       kinematiccontrollerbase_1_chip_id, kinematiccontrollerbase_1_leftbaryout,
       kinematiccontrollerbase_1_rightbaryout, process_1_rightbat, videosection_1_outballx,
       videosection_1_outbally, videosection_1_outchipid, videosection_1_outleftbary,
       videosection_1_outrightbary, videosection_2_outballx, videosection_2_outbally,
       videosection_2_outchipid, videosection_2_outleftbary, videosection_2_outrightbary,
       videosection_3_outballx, videosection_3_outbally, videosection_3_outchipid,
       videosection_3_outleftbary, videosection_3_outrightbary;
  wire [6:0] win_mode_1__1, win_mode_1__2, win_mode_1__3, win_mode_1__4, win_mode_1__5, win_mode_1__6,
       win_mode_1__7, win_mode_1__8, win_mode_1__9, win_mode_1__10, win_mode_1__11, win_mode_1__12,
       win_mode_1__13, win_mode_1__14, win_mode_1__15, win_mode_1__16, win_mode_1__17, win_mode_1__18,
       win_mode_1__19, win_mode_1__20, win_mode_1__21, win_mode_1__22, win_mode_1__23, win_mode_1__24,
       win_mode_1__25, win_mode_1__26, win_mode_1__27, win_mode_1__28, win_mode_1__29, win_mode_1__30,
       win_mode_1__31, win_mode_1__32;
  wire [7:0] kinematiccontrollerbase_1_scoreleft, kinematiccontrollerbase_1_scoreright,
       kinematiccontrollerbase_1_vxy, kinematiccontrollerbase_1_xprocess, kinematiccontrollerbase_1_yprocess;
  wire [31:0] videosection_1_col0, videosection_1_col1, videosection_1_col2, videosection_1_col3,
       videosection_1_col4, videosection_1_col5, videosection_1_col6, videosection_1_col7,
       videosection_2_col0, videosection_2_col1, videosection_2_col2, videosection_2_col3,
       videosection_2_col4, videosection_2_col5, videosection_2_col6, videosection_2_col7,
       videosection_3_col0, videosection_3_col1, videosection_3_col2, videosection_3_col3,
       videosection_3_col4, videosection_3_col5, videosection_3_col6, videosection_3_col7,
       videosection_4_col0, videosection_4_col1, videosection_4_col2, videosection_4_col3,
       videosection_4_col4, videosection_4_col5, videosection_4_col6, videosection_4_col7;

  Process process_1 (
    .rightbat(process_1_rightbat), .BallX(kinematiccontrollerbase_1_xprocess),
    .BallY(kinematiccontrollerbase_1_yprocess), .vxy(kinematiccontrollerbase_1_vxy));
  Hex_Digit_Display hex_digit_display_1 (.value(binaryto3dig_1_hundreds));  // open: dp
  Hex_Digit_Display hex_digit_display_2 (.value(binaryto3dig_1_tens));  // open: dp
  Joystick #(.bits(5)) joystick_1 (.y(joystick_1_y));  // open: x
  CorrectJoystik correctjoystik_1 (.Joystik(joystick_1_y), .JoystikOut(joystik));
  Button u_MODE (.out(mode));
  Button AGAIN (.out(AGAIN_out));
  DotMatrix #(.matrixcols(32)) dotmatrix_1 (
    .col0(win_mode_1__1), .col1(win_mode_1__2), .col2(win_mode_1__3), .col3(win_mode_1__4),
    .col4(win_mode_1__5), .col5(win_mode_1__6), .col6(win_mode_1__7), .col7(win_mode_1__8),
    .col8(win_mode_1__9), .col9(win_mode_1__10), .col10(win_mode_1__11), .col11(win_mode_1__12),
    .col12(win_mode_1__13), .col13(win_mode_1__14), .col14(win_mode_1__15), .col15(win_mode_1__16),
    .col16(win_mode_1__17), .col17(win_mode_1__18), .col18(win_mode_1__19), .col19(win_mode_1__20),
    .col20(win_mode_1__21), .col21(win_mode_1__22), .col22(win_mode_1__23), .col23(win_mode_1__24),
    .col24(win_mode_1__25), .col25(win_mode_1__26), .col26(win_mode_1__27), .col27(win_mode_1__28),
    .col28(win_mode_1__29), .col29(win_mode_1__30), .col30(win_mode_1__31), .col31(win_mode_1__32));
  Win_Mode win_mode_1 (
    .Mode(modeout), .WinLeft(winleft), .WinRight(winright), ._1(win_mode_1__1), ._9(win_mode_1__9),
    ._17(win_mode_1__17), ._25(win_mode_1__25), ._2(win_mode_1__2), ._10(win_mode_1__10),
    ._18(win_mode_1__18), ._26(win_mode_1__26), ._3(win_mode_1__3), ._11(win_mode_1__11),
    ._19(win_mode_1__19), ._27(win_mode_1__27), ._4(win_mode_1__4), ._12(win_mode_1__12),
    ._20(win_mode_1__20), ._28(win_mode_1__28), ._5(win_mode_1__5), ._13(win_mode_1__13),
    ._21(win_mode_1__21), ._29(win_mode_1__29), ._6(win_mode_1__6), ._14(win_mode_1__14),
    ._22(win_mode_1__22), ._30(win_mode_1__30), ._7(win_mode_1__7), ._15(win_mode_1__15),
    ._23(win_mode_1__23), ._31(win_mode_1__31), ._8(win_mode_1__8), ._16(win_mode_1__16),
    ._24(win_mode_1__24), ._32(win_mode_1__32));
  Hex_Digit_Display hex_digit_display_3 (.value(binaryto3dig_1_ones));  // open: dp
  Binaryto3Dig binaryto3dig_1 (
    .number(kinematiccontrollerbase_1_scoreleft), .hundreds(binaryto3dig_1_hundreds),
    .tens(binaryto3dig_1_tens), .ones(binaryto3dig_1_ones));
  DotMatrix #(.matrixcols(32), .matrixrows(32)) dotmatrix_2 (
    .col0(videosection_1_col0), .col1(videosection_1_col1), .col2(videosection_1_col2),
    .col3(videosection_1_col3), .col4(videosection_1_col4), .col5(videosection_1_col5),
    .col6(videosection_1_col6), .col7(videosection_1_col7), .col8(videosection_2_col0),
    .col9(videosection_2_col1), .col10(videosection_2_col2), .col11(videosection_2_col3),
    .col12(videosection_2_col4), .col13(videosection_2_col5), .col14(videosection_2_col6),
    .col15(videosection_2_col7), .col16(videosection_3_col0), .col17(videosection_3_col1),
    .col18(videosection_3_col2), .col19(videosection_3_col3), .col20(videosection_3_col4),
    .col21(videosection_3_col5), .col22(videosection_3_col6), .col23(videosection_3_col7),
    .col24(videosection_4_col0), .col25(videosection_4_col1), .col26(videosection_4_col2),
    .col27(videosection_4_col3), .col28(videosection_4_col4), .col29(videosection_4_col5),
    .col30(videosection_4_col6), .col31(videosection_4_col7));
  VideoSection videosection_1 (
    .BallX(kinematiccontrollerbase_1_ballxout), .BallY(kinematiccontrollerbase_1_ballyout),
    .LeftbarY(kinematiccontrollerbase_1_leftbaryout), .RightbarY(kinematiccontrollerbase_1_rightbaryout),
    .col1(videosection_1_col1), .col3(videosection_1_col3), .col5(videosection_1_col5),
    .col7(videosection_1_col7), .col0(videosection_1_col0), .col2(videosection_1_col2),
    .col4(videosection_1_col4), .col6(videosection_1_col6), .OutBallX(videosection_1_outballx),
    .OutBallY(videosection_1_outbally), .OutLeftbarY(videosection_1_outleftbary),
    .OutRightbarY(videosection_1_outrightbary), .ChipID(kinematiccontrollerbase_1_chip_id),
    .OutChipID(videosection_1_outchipid));
  KinematicControllerBase kinematiccontrollerbase_1 (
    .Reset(AGAIN_out), .RightbarY(process_1_rightbat), .BallXout(kinematiccontrollerbase_1_ballxout),
    .BallYout(kinematiccontrollerbase_1_ballyout), .Chip_ID(kinematiccontrollerbase_1_chip_id),
    .XProcess(kinematiccontrollerbase_1_xprocess), .YProcess(kinematiccontrollerbase_1_yprocess),
    .VXY(kinematiccontrollerbase_1_vxy), .mode(mode), .modeout(modeout), .winleft(winleft),
    .winright(winright), .RightbarYOut(kinematiccontrollerbase_1_rightbaryout),
    .LeftbarYOut(kinematiccontrollerbase_1_leftbaryout), .LeftbarY(joystik),
    .ScoreLeft(kinematiccontrollerbase_1_scoreleft), .ScoreRight(kinematiccontrollerbase_1_scoreright));
  VideoSection videosection_2 (
    .BallX(videosection_1_outballx), .BallY(videosection_1_outbally), .LeftbarY(videosection_1_outleftbary),
    .RightbarY(videosection_1_outrightbary), .col1(videosection_2_col1), .col3(videosection_2_col3),
    .col5(videosection_2_col5), .col7(videosection_2_col7), .col0(videosection_2_col0),
    .col2(videosection_2_col2), .col4(videosection_2_col4), .col6(videosection_2_col6),
    .OutBallX(videosection_2_outballx), .OutBallY(videosection_2_outbally),
    .OutLeftbarY(videosection_2_outleftbary), .OutRightbarY(videosection_2_outrightbary),
    .ChipID(videosection_1_outchipid), .OutChipID(videosection_2_outchipid));
  VideoSection videosection_3 (
    .BallX(videosection_2_outballx), .BallY(videosection_2_outbally), .LeftbarY(videosection_2_outleftbary),
    .RightbarY(videosection_2_outrightbary), .col1(videosection_3_col1), .col3(videosection_3_col3),
    .col5(videosection_3_col5), .col7(videosection_3_col7), .col0(videosection_3_col0),
    .col2(videosection_3_col2), .col4(videosection_3_col4), .col6(videosection_3_col6),
    .OutBallX(videosection_3_outballx), .OutBallY(videosection_3_outbally),
    .OutLeftbarY(videosection_3_outleftbary), .OutRightbarY(videosection_3_outrightbary),
    .ChipID(videosection_2_outchipid), .OutChipID(videosection_3_outchipid));
  VideoSection videosection_4 (
    .BallX(videosection_3_outballx), .BallY(videosection_3_outbally), .LeftbarY(videosection_3_outleftbary),
    .RightbarY(videosection_3_outrightbary), .col1(videosection_4_col1), .col3(videosection_4_col3),
    .col5(videosection_4_col5), .col7(videosection_4_col7), .col0(videosection_4_col0),
    .col2(videosection_4_col2), .col4(videosection_4_col4), .col6(videosection_4_col6),
    .ChipID(videosection_3_outchipid));  // open: OutBallX, OutBallY, OutLeftbarY, OutRightbarY, OutChipID
  Hex_Digit_Display hex_digit_display_4 (.value(binaryto3dig_2_hundreds));  // open: dp
  Binaryto3Dig binaryto3dig_2 (
    .number(kinematiccontrollerbase_1_scoreright), .hundreds(binaryto3dig_2_hundreds),
    .tens(binaryto3dig_2_tens), .ones(binaryto3dig_2_ones));
  Hex_Digit_Display hex_digit_display_5 (.value(binaryto3dig_2_ones));  // open: dp
  Hex_Digit_Display hex_digit_display_6 (.value(binaryto3dig_2_tens));  // open: dp
endmodule

module VideoChip (
  input  [4:0] LeftbatY,
  input  [4:0] RightbatY,
  input  [4:0] BallY,
  input  [4:0] ChipID,
  input  [4:0] BallX,
  output [4:0] OutLeftbatY,
  output [31:0] Display,
  output [4:0] OutRightbatY,
  output [4:0] OutBallY,
  output [4:0] OutChipID,
  output [4:0] OutBallX
);

  wire and_1_out, and_2_out, equal5bits_1_result;
  wire [31:0] and_3_out, and_4_out, and_5_out, bit_extender_1_out, bit_extender_2_out, bit_extender_3_out,
       shifter_1_out, shifter_2_out, shifter_3_out;

  and and_1 (and_1_out, ~ChipID[0], ~ChipID[1], ChipID[2], ChipID[3], ChipID[4]);  // AND_Gate
  Inc5bits inc5bits_1 (.X(ChipID), .X_1(OutChipID));  // open: Cout
  and and_2 (and_2_out, ChipID[0], ChipID[1], ~ChipID[2], ~ChipID[3], ~ChipID[4]);  // AND_Gate
  Equal5Bits equal5bits_1 (.A(ChipID), .B(BallX), .result(equal5bits_1_result));
  Shifter #(.width(32)) shifter_1 (.in(32'h7), .\dist (LeftbatY), .out(shifter_1_out));
  assign bit_extender_1_out = {{31{and_2_out}}, and_2_out};  // Bit_Extender bit_extender_1
  Shifter #(.width(32)) shifter_2 (.in(32'h7), .\dist (RightbatY), .out(shifter_2_out));
  assign bit_extender_2_out = {{31{and_1_out}}, and_1_out};  // Bit_Extender bit_extender_2
  Shifter #(.width(32)) shifter_3 (.in(32'h1), .\dist (BallY), .out(shifter_3_out));
  assign bit_extender_3_out = {{31{equal5bits_1_result}}, equal5bits_1_result};  // Bit_Extender bit_extender_3
  assign and_3_out = shifter_1_out & bit_extender_1_out;  // AND_Gate and_3, 32 bits wide
  assign and_4_out = shifter_2_out & bit_extender_2_out;  // AND_Gate and_4, 32 bits wide
  assign and_5_out = shifter_3_out & bit_extender_3_out;  // AND_Gate and_5, 32 bits wide
  assign Display = and_3_out | and_4_out | and_5_out;  // OR_Gate or_1, 32 bits wide

  assign OutBallX = BallX;
  assign OutBallY = BallY;
  assign OutLeftbatY = LeftbatY;
  assign OutRightbatY = RightbatY;

  // Notes on the sheet:
  //   ChipID == 3?
  //   ChipID == 28?
  //   Show left bat
  //   Show right bat
  //   Show ball
endmodule

module VideoSection (
  input  [4:0] ChipID,
  input  [4:0] BallX,
  input  [4:0] BallY,
  input  [4:0] LeftbarY,
  input  [4:0] RightbarY,
  output [31:0] col1,
  output [31:0] col3,
  output [31:0] col5,
  output [31:0] col7,
  output [31:0] col0,
  output [31:0] col2,
  output [31:0] col4,
  output [31:0] col6,
  output [4:0] OutChipID,
  output [4:0] OutBallX,
  output [4:0] OutBallY,
  output [4:0] OutLeftbarY,
  output [4:0] OutRightbarY
);

  wire [4:0] videochip_1_outballx, videochip_1_outbally, videochip_1_outchipid, videochip_1_outleftbaty,
       videochip_1_outrightbaty, videochip_2_outballx, videochip_2_outbally, videochip_2_outchipid,
       videochip_2_outleftbaty, videochip_2_outrightbaty, videochip_3_outballx, videochip_3_outbally,
       videochip_3_outchipid, videochip_3_outleftbaty, videochip_3_outrightbaty, videochip_4_outballx,
       videochip_4_outbally, videochip_4_outchipid, videochip_4_outleftbaty, videochip_4_outrightbaty,
       videochip_5_outballx, videochip_5_outbally, videochip_5_outchipid, videochip_5_outleftbaty,
       videochip_5_outrightbaty, videochip_6_outballx, videochip_6_outbally, videochip_6_outchipid,
       videochip_6_outleftbaty, videochip_6_outrightbaty, videochip_8_outballx, videochip_8_outbally,
       videochip_8_outchipid, videochip_8_outleftbaty, videochip_8_outrightbaty;

  VideoChip videochip_1 (
    .LeftbatY(LeftbarY), .OutLeftbatY(videochip_1_outleftbaty), .RightbatY(RightbarY),
    .OutRightbatY(videochip_1_outrightbaty), .BallY(BallY), .OutBallY(videochip_1_outbally), .ChipID(ChipID),
    .BallX(BallX), .Display(col0), .OutChipID(videochip_1_outchipid), .OutBallX(videochip_1_outballx));
  VideoChip videochip_2 (
    .LeftbatY(videochip_1_outleftbaty), .OutLeftbatY(videochip_2_outleftbaty),
    .RightbatY(videochip_1_outrightbaty), .OutRightbatY(videochip_2_outrightbaty),
    .BallY(videochip_1_outbally), .OutBallY(videochip_2_outbally), .ChipID(videochip_1_outchipid),
    .BallX(videochip_1_outballx), .Display(col1), .OutChipID(videochip_2_outchipid),
    .OutBallX(videochip_2_outballx));
  VideoChip videochip_3 (
    .LeftbatY(videochip_2_outleftbaty), .OutLeftbatY(videochip_3_outleftbaty),
    .RightbatY(videochip_2_outrightbaty), .OutRightbatY(videochip_3_outrightbaty),
    .BallY(videochip_2_outbally), .OutBallY(videochip_3_outbally), .ChipID(videochip_2_outchipid),
    .BallX(videochip_2_outballx), .Display(col2), .OutChipID(videochip_3_outchipid),
    .OutBallX(videochip_3_outballx));
  VideoChip videochip_4 (
    .LeftbatY(videochip_5_outleftbaty), .OutLeftbatY(videochip_4_outleftbaty),
    .RightbatY(videochip_5_outrightbaty), .OutRightbatY(videochip_4_outrightbaty),
    .BallY(videochip_5_outbally), .OutBallY(videochip_4_outbally), .ChipID(videochip_5_outchipid),
    .BallX(videochip_5_outballx), .Display(col4), .OutChipID(videochip_4_outchipid),
    .OutBallX(videochip_4_outballx));
  VideoChip videochip_5 (
    .LeftbatY(videochip_3_outleftbaty), .OutLeftbatY(videochip_5_outleftbaty),
    .RightbatY(videochip_3_outrightbaty), .OutRightbatY(videochip_5_outrightbaty),
    .BallY(videochip_3_outbally), .OutBallY(videochip_5_outbally), .ChipID(videochip_3_outchipid),
    .BallX(videochip_3_outballx), .Display(col3), .OutChipID(videochip_5_outchipid),
    .OutBallX(videochip_5_outballx));
  VideoChip videochip_6 (
    .LeftbatY(videochip_4_outleftbaty), .OutLeftbatY(videochip_6_outleftbaty),
    .RightbatY(videochip_4_outrightbaty), .OutRightbatY(videochip_6_outrightbaty),
    .BallY(videochip_4_outbally), .OutBallY(videochip_6_outbally), .ChipID(videochip_4_outchipid),
    .BallX(videochip_4_outballx), .Display(col5), .OutChipID(videochip_6_outchipid),
    .OutBallX(videochip_6_outballx));
  VideoChip videochip_7 (
    .LeftbatY(videochip_8_outleftbaty), .OutLeftbatY(OutLeftbarY), .RightbatY(videochip_8_outrightbaty),
    .OutRightbatY(OutRightbarY), .BallY(videochip_8_outbally), .OutBallY(OutBallY),
    .ChipID(videochip_8_outchipid), .BallX(videochip_8_outballx), .Display(col7), .OutChipID(OutChipID),
    .OutBallX(OutBallX));
  VideoChip videochip_8 (
    .LeftbatY(videochip_6_outleftbaty), .OutLeftbatY(videochip_8_outleftbaty),
    .RightbatY(videochip_6_outrightbaty), .OutRightbatY(videochip_8_outrightbaty),
    .BallY(videochip_6_outbally), .OutBallY(videochip_8_outbally), .ChipID(videochip_6_outchipid),
    .BallX(videochip_6_outballx), .Display(col6), .OutChipID(videochip_8_outchipid),
    .OutBallX(videochip_8_outballx));
endmodule

module Reflect (
  input  [2:0] oldv,
  output [2:0] newv
);

  wire and_2_out;
  wire [2:0] and_1_out, not_1_out, not_2_out, xnor_1_out, xor_1_out;

  assign not_1_out = ~oldv;  // NOT_Gate not_1, 3 bits wide
  assign and_1_out = {and_1_out[1:0], 1'b1} & not_1_out;  // AND_Gate and_1, 3 bits wide
  assign xor_1_out = not_1_out ^ {and_1_out[1:0], 1'b1};  // XOR_Gate xor_1, 3 bits wide
  assign not_2_out = ~oldv;  // NOT_Gate not_2, 3 bits wide
  assign xnor_1_out = ~(oldv ^ 3'b100);  // XNOR_Gate xnor_1, 3 bits wide
  and and_2 (and_2_out, xnor_1_out[0], xnor_1_out[1], xnor_1_out[2]);
  Multiplexer #(.width(3), .enable("false")) multiplexer_1 (
    .in0(xor_1_out), .in1(not_2_out), .out(newv), .sel(and_2_out));

  // Notes on the sheet:
  //   Change speed of ball
  //   -(-4) = 3
  //   Neg x (not x + 1)
endmodule

module Inrange (
  input  [4:0] Ybat,
  input  [4:0] Yball,
  output shareArrow
);

  wire equal5bits_1_result, equal5bits_2_result, equal5bits_3_result;
  wire [4:0] inc5bits_1_x_1, inc5bits_2_x_1;

  Inc5bits inc5bits_1 (.X(Ybat), .X_1(inc5bits_1_x_1));  // open: Cout
  Inc5bits inc5bits_2 (.X(inc5bits_1_x_1), .X_1(inc5bits_2_x_1));  // open: Cout
  Equal5Bits equal5bits_1 (.A(Ybat), .B(Yball), .result(equal5bits_1_result));
  Equal5Bits equal5bits_2 (.A(Yball), .B(inc5bits_1_x_1), .result(equal5bits_2_result));
  Equal5Bits equal5bits_3 (.A(Yball), .B(inc5bits_2_x_1), .result(equal5bits_3_result));
  or or_1 (shareArrow, equal5bits_1_result, equal5bits_2_result, equal5bits_3_result);

  // Notes on the sheet:
  //   Is the ball in the same line with the bat?
endmodule

module KinematicControllerBase (
  input  mode,
  input  Reset,
  input  [4:0] LeftbarY,
  input  [4:0] RightbarY,
  output modeout,
  output [4:0] Chip_ID,
  output [7:0] VXY,
  output [4:0] BallXout,
  output [7:0] XProcess,
  output [4:0] BallYout,
  output [7:0] YProcess,
  output [4:0] LeftbarYOut,
  output [4:0] RightbarYOut,
  output [7:0] ScoreLeft,
  output winleft,
  output [7:0] ScoreRight,
  output winright
);

  wire adder_1_cout, adder_2_cout, adder_5_cout, adder_6_cout, adder_9_cout, and_1_out, and_2_out, and_3_out,
       and_4_out, and_5_out, and_6_out, and_7_out, and_8_out, and_9_out, and_10_out, and_11_out, and_12_out,
       and_13_out, and_14_out, and_16_out, bats_1_minusleft, bats_1_minusright, bats_1_plusleft,
       bats_1_plusright, Clock, clock_1_out, d_ff_1_q, d_ff_3_q, d_ff_4_q, equal5bits_1_result,
       equal5bits_2_result, equal5bits_3_result, equal5bits_4_result, inrange_1_sharearrow,
       inrange_2_sharearrow, or_1_out, or_2_out, or_4_out, or_5_out, or_6_out, or_7_out, or_8_out, or_9_out,
       or_10_out, or_11_out, or_12_out, or_13_out, Reset_t, ResetMode, xor_1_out, xor_2_out, xor_3_out,
       xor_4_out;
  wire [2:0] adder_1_out, batreflectvy_1_speedout, diffusion_1_speedout, multiplexer_1_out,
       multiplexer_2_out, multiplexer_3_out, multiplexer_4_out, multiplexer_5_out, multiplexer_6_out,
       multiplexer_7_out, multiplexer_8_out, multiplexer_9_out, multiplexer_10_out, multiplexer_11_out,
       multiplexer_12_out, multiplexer_13_out, multiplexer_16_out, multiplexer_17_out, reflect_1_newv,
       reflect_2_newv, subtractor_1_out, VXreg_q, Xreg_q, Yreg_2_q;
  wire [4:0] adder_7_out, adder_8_out;
  wire [5:3] VYreg_q;
  wire [7:0] adder_2_out, adder_3_out, adder_4_out, adder_9_out, bit_extender_1_out, bit_extender_2_out,
       multiplexer_14_out, multiplexer_15_out, multiplexer_18_out, multiplexer_19_out, not_1_out, Yreg_q;

  Adder #(.width(3)) adder_1 (.a(reflect_1_newv), .b(3'b001), .out(adder_1_out), .cout(adder_1_cout));  // open: cin
  Multiplexer #(.width(3), .enable("false")) multiplexer_1 (
    .in0(reflect_1_newv), .in1(adder_1_out), .out(multiplexer_1_out), .sel(bats_1_plusright));
  Subtractor #(.width(3)) subtractor_1 (.a(reflect_1_newv), .b(3'b001), .out(subtractor_1_out));  // open: bin, bout
  Multiplexer #(.width(3), .enable("false")) multiplexer_2 (
    .in0(reflect_1_newv), .in1(adder_1_out), .out(multiplexer_2_out), .sel(bats_1_plusleft));
  Multiplexer #(.width(3), .enable("false")) multiplexer_3 (
    .in0(reflect_1_newv), .in1(multiplexer_4_out), .out(multiplexer_3_out), .sel(and_4_out));
  Multiplexer #(.width(3), .enable("false")) multiplexer_4 (
    .in0(multiplexer_1_out), .in1(subtractor_1_out), .out(multiplexer_4_out), .sel(bats_1_minusright));
  Multiplexer #(.width(3), .enable("false")) multiplexer_5 (
    .in0(reflect_1_newv), .in1(multiplexer_6_out), .out(multiplexer_5_out), .sel(and_5_out));
  Multiplexer #(.width(3), .enable("false")) multiplexer_6 (
    .in0(multiplexer_2_out), .in1(subtractor_1_out), .out(multiplexer_6_out), .sel(bats_1_minusleft));
  Bats bats_1 (
    .LeftbarY(LeftbarY), .LeftbarYOut(LeftbarYOut), .RightbarY(RightbarY), .RightbarYOut(RightbarYOut),
    .clock(Clock), .plusleft(bats_1_plusleft), .minusleft(bats_1_minusleft), .plusright(bats_1_plusright),
    .minusright(bats_1_minusright));
  and and_1 (and_1_out, ~multiplexer_3_out[0], ~multiplexer_3_out[1], ~multiplexer_3_out[2]);  // AND_Gate
  and and_2 (and_2_out, ~multiplexer_5_out[0], ~multiplexer_5_out[1], ~multiplexer_5_out[2]);  // AND_Gate
  Multiplexer #(.width(3), .enable("false")) multiplexer_7 (
    .in0(multiplexer_3_out), .in1(reflect_1_newv), .out(multiplexer_7_out), .sel(or_1_out));
  or or_1 (or_1_out, and_1_out, adder_1_cout);
  Multiplexer #(.width(3), .enable("false")) multiplexer_8 (
    .in0(multiplexer_7_out), .in1(multiplexer_9_out), .out(multiplexer_8_out), .sel(and_5_out));
  // Probe on multiplexer_8_out
  Multiplexer #(.width(3), .enable("false")) multiplexer_9 (
    .in0(multiplexer_5_out), .in1(reflect_1_newv), .out(multiplexer_9_out), .sel(or_2_out));
  or or_2 (or_2_out, and_2_out, adder_1_cout);
  // Probe on VXreg_q
  Reflect reflect_1 (.oldv(VXreg_q), .newv(reflect_1_newv));
  Multiplexer #(.width(3), .enable("false")) multiplexer_10 (
    .in0(reflect_1_newv), .in1(multiplexer_8_out), .out(multiplexer_10_out), .sel(or_6_out));
  Multiplexer #(.width(3), .enable("false")) multiplexer_11 (
    .in0(VXreg_q), .in1(multiplexer_10_out), .out(multiplexer_11_out), .sel(or_5_out));
  Multiplexer #(.width(3), .enable("false")) multiplexer_12 (
    .in0(multiplexer_11_out), .in1(multiplexer_13_out), .out(multiplexer_12_out), .sel(ResetMode));
  Register #(.width(3)) VXreg (.D(multiplexer_12_out), .Q(VXreg_q), .clk(Clock));  // open: en, clr
  Multiplexer #(.width(3), .enable("false")) multiplexer_13 (
    .in0(3'b110), .in1(3'b010), .out(multiplexer_13_out), .sel(and_9_out));
  Counter #(.width(1), .max('h1)) counter_1 (.Q(modeout), .clk(mode));  // open: load, D, count, carry, clr
  assign bit_extender_1_out = {{5{VXreg_q[2]}}, VXreg_q};  // Bit_Extender bit_extender_1
  or or_3 (Reset_t, mode, Reset);
  Adder adder_2 (.a(bit_extender_1_out), .b({BallXout, Xreg_q}), .out(adder_2_out), .cout(adder_2_cout));  // open: cin
  Multiplexer #(.width(8), .enable("false")) multiplexer_14 (
    .in0(8'hd4), .in1(8'h28), .out(multiplexer_14_out), .sel(and_9_out));
  and and_3 (and_3_out, ~or_5_out, ~or_6_out);  // AND_Gate
  Multiplexer #(.width(8), .enable("false")) multiplexer_15 (
    .in0(adder_2_out), .in1(multiplexer_14_out), .out(multiplexer_15_out), .sel(ResetMode));
  or or_4 (or_4_out, and_3_out, ResetMode);
  Register #(.trigger("falling")) Xreg (
    .D(multiplexer_15_out), .en(or_4_out), .Q({BallXout, Xreg_q}), .clk(Clock));  // open: clr
  Adder adder_3 (.a({BallXout, Xreg_q}), .b(8'h1c), .out(adder_3_out));  // open: cin, cout
  Adder adder_4 (.a({BallXout, Xreg_q}), .b(8'he4), .out(adder_4_out));  // open: cin, cout
  Register #(.trigger("falling")) register_1 (
    .D({BallXout, Xreg_q}), .en(and_16_out), .Q(XProcess), .clk(Clock));  // open: clr
  or or_5 (or_5_out, or_6_out, xor_2_out);
  Adder adder_5 (.a(adder_3_out), .b(bit_extender_1_out), .cout(adder_5_cout));  // open: out, cin
  Adder adder_6 (.a(adder_4_out), .b(bit_extender_1_out), .cout(adder_6_cout));  // open: out, cin
  xor xor_1 (xor_1_out, adder_6_cout, VXreg_q[2]);
  Inrange inrange_1 (.Yball(BallYout), .Ybat(LeftbarYOut), .shareArrow(inrange_1_sharearrow));
  xor xor_2 (xor_2_out, adder_2_cout, VXreg_q[2]);
  xor xor_3 (xor_3_out, adder_5_cout, VXreg_q[2]);
  and and_4 (and_4_out, xor_3_out, inrange_2_sharearrow);
  Inrange inrange_2 (.Yball(BallYout), .Ybat(RightbarYOut), .shareArrow(inrange_2_sharearrow));
  and and_5 (and_5_out, xor_1_out, inrange_1_sharearrow);
  and and_6 (and_6_out, xor_2_out, ~VXreg_q[2]);  // AND_Gate
  and and_7 (and_7_out, xor_2_out, VXreg_q[2]);
  or or_6 (or_6_out, and_4_out, and_5_out);
  Adder #(.width(5)) adder_7 (.a(LeftbarYOut), .b(5'b00010), .out(adder_7_out));  // open: cin, cout
  D_Flip_Flop d_ff_1 (.clk(Clock), .D(and_6_out), .Q(d_ff_1_q));  // open: Qn, preset, en, reset
  or or_7 (or_7_out, and_6_out, and_7_out);
  and and_8 (and_8_out, and_5_out, equal5bits_1_result);
  Equal5Bits equal5bits_1 (.A(BallYout), .B(LeftbarYOut), .result(equal5bits_1_result));
  Equal5Bits equal5bits_2 (.A(BallYout), .B(adder_7_out), .result(equal5bits_2_result));
  Equal5Bits equal5bits_3 (.A(BallYout), .B(RightbarYOut), .result(equal5bits_3_result));
  Equal5Bits equal5bits_4 (.A(BallYout), .B(adder_8_out), .result(equal5bits_4_result));
  Adder #(.width(5)) adder_8 (.a(RightbarYOut), .b(5'b00010), .out(adder_8_out));  // open: cin, cout
  and and_9 (and_9_out, ~modeout, d_ff_1_q);  // AND_Gate
  and and_10 (and_10_out, ~modeout, or_7_out);  // AND_Gate
  or or_8 (or_8_out, and_10_out, Reset_t);
  and and_11 (and_11_out, and_5_out, equal5bits_2_result);
  and and_12 (and_12_out, equal5bits_3_result, and_4_out);
  and and_13 (and_13_out, and_4_out, equal5bits_4_result);
  D_Flip_Flop d_ff_2 (.clk(Clock), .D(or_8_out), .Q(ResetMode));  // open: Qn, preset, en, reset
  Register #(.trigger("falling")) register_2 (
    .D({2'b00, VYreg_q, VXreg_q}), .en(and_16_out), .Q(VXY), .clk(Clock));  // open: clr
  or or_9 (or_9_out, and_8_out, and_12_out);
  Reflect reflect_2 (.oldv(VYreg_q), .newv(reflect_2_newv));
  or or_10 (or_10_out, and_11_out, and_13_out);
  Multiplexer #(.width(3), .enable("false")) multiplexer_16 (
    .in0(VYreg_q), .in1(diffusion_1_speedout), .out(multiplexer_16_out), .sel(xor_4_out));
  Diffusion diffusion_1 (.Speed(reflect_2_newv), .SpeedOut(diffusion_1_speedout), .clock(Clock), .mode(modeout));
  xor xor_4 (xor_4_out, VYreg_q[5], adder_9_cout);
  BatReflectVy batreflectvy_1 (
    .Speed(multiplexer_16_out), .SpeedOut(batreflectvy_1_speedout), .up(or_10_out), .down(or_9_out));
  Multiplexer #(.width(3), .enable("false")) multiplexer_17 (
    .in0(batreflectvy_1_speedout), .in1(3'b001), .out(multiplexer_17_out), .sel(ResetMode));
  D_Flip_Flop d_ff_3 (.clk(Clock), .D(xor_4_out), .Q(d_ff_3_q));  // open: Qn, preset, en, reset
  Score score_1 (
    .wall(and_6_out), .clock(Clock), .reset(Reset_t), .mode(modeout), .resscore(or_13_out),
    .Score(ScoreLeft), .max(winleft));
  Score score_2 (
    .wall(and_7_out), .clock(Clock), .reset(Reset_t), .mode(modeout), .resscore(or_13_out),
    .Score(ScoreRight), .max(winright));
  Register #(.width(3)) VYreg (.D(multiplexer_17_out), .Q(VYreg_q), .clk(Clock));  // open: en, clr
  assign bit_extender_2_out = {{5{VYreg_q[5]}}, VYreg_q};  // Bit_Extender bit_extender_2
  Adder adder_9 (
    .a(bit_extender_2_out), .b({BallYout, Yreg_2_q}), .out(adder_9_out), .cout(adder_9_cout));  // open: cin
  Register Yreg (.D(adder_9_out), .Q(Yreg_q), .clk(Clock));  // open: en, clr
  assign not_1_out = ~Yreg_q;  // NOT_Gate not_1, 8 bits wide
  and and_14 (and_14_out, ~modeout, or_11_out);  // AND_Gate
  or or_11 (or_11_out, winleft, winright);
  or or_12 (or_12_out, and_9_out, or_6_out, xor_4_out, and_7_out);
  Multiplexer #(.width(8), .enable("false")) multiplexer_18 (
    .in0(multiplexer_19_out), .in1(8'h80), .out(multiplexer_18_out), .sel(ResetMode));
  Register #(.trigger("falling")) Yreg_2 (
    .D(multiplexer_18_out), .Q({BallYout, Yreg_2_q}), .clk(Clock));  // open: en, clr
  Multiplexer #(.width(8), .enable("false")) multiplexer_19 (
    .in0(adder_9_out), .in1(not_1_out), .out(multiplexer_19_out), .sel(d_ff_3_q));
  Clock #(.highDuration(10), .lowDuration(10)) clock_1 (.out(clock_1_out));
  or or_13 (or_13_out, and_14_out, Reset_t);
  D_Flip_Flop d_ff_4 (.clk(Clock), .D(or_12_out), .Q(d_ff_4_q));  // open: Qn, preset, en, reset
  and and_15 (Clock, clock_1_out, ~and_14_out);  // AND_Gate
  and and_16 (and_16_out, ~VXreg_q[2], ~BallXout[4], d_ff_4_q);  // AND_Gate
  Register #(.trigger("falling")) register_3 (
    .D({BallYout, Yreg_2_q}), .en(and_16_out), .Q(YProcess), .clk(Clock));  // open: clr

  assign Chip_ID = {5{1'b0}};

  // Other names for the same wires on the sheet: mode_t = modeout

  // Notes on the sheet:
  //   Change VX
  //   Left Wall
  //   Right Bat
  //   Ball hit bat
  //   Left bat
  //   Right wall
  //   Reset + MODE + IN/OUT
  //   Out for robot
endmodule

module Process (
  input  [7:0] BallX,
  input  [7:0] BallY,
  input  [7:0] vxy,
  output [4:0] rightbat
);

  wire and_1_out, and_2_out, and_3_out, and_4_out, and_5_out, and_6_out, cdm_8_mark5_1_p2, cdm_8_mark5_1_p3,
       clock_1_out, not_1_out, not_2_out;
  wire [2:0] register_1_q;
  wire [7:0] cdm_8_mark5_1_p4, cdm_8_mark5_1_p5, cdm_8_mark5_1_p6, controlled_buffer_1_out,
       controlled_buffer_3_out;

  Clock clock_1 (.out(clock_1_out));
  // CdM_8_mark5 cdm_8_mark5_1: pin names not known; wires that end beside it: clock_1_out, cdm_8_mark5_1_p2, cdm_8_mark5_1_p3, cdm_8_mark5_1_p4, cdm_8_mark5_1_p5, cdm_8_mark5_1_p6
  assign controlled_buffer_1_out = not_1_out ? cdm_8_mark5_1_p5 : 8'bz;  // Controlled_Buffer controlled_buffer_1
  not not_1 (not_1_out, cdm_8_mark5_1_p3);
  assign cdm_8_mark5_1_p6 = cdm_8_mark5_1_p3 ? controlled_buffer_1_out : 8'bz;  // Controlled_Buffer controlled_buffer_2
  and and_1 (and_1_out, cdm_8_mark5_1_p4[0], cdm_8_mark5_1_p4[1], ~cdm_8_mark5_1_p4[2], ~cdm_8_mark5_1_p4[3], cdm_8_mark5_1_p4[4], cdm_8_mark5_1_p4[5], cdm_8_mark5_1_p4[6], cdm_8_mark5_1_p4[7]);  // AND_Gate
  and and_2 (and_2_out, ~cdm_8_mark5_1_p4[0], ~cdm_8_mark5_1_p4[1], cdm_8_mark5_1_p4[2], ~cdm_8_mark5_1_p4[3], cdm_8_mark5_1_p4[4], cdm_8_mark5_1_p4[5], cdm_8_mark5_1_p4[6], cdm_8_mark5_1_p4[7], cdm_8_mark5_1_p3, cdm_8_mark5_1_p2);  // AND_Gate
  and and_3 (and_3_out, cdm_8_mark5_1_p4[0], ~cdm_8_mark5_1_p4[1], cdm_8_mark5_1_p4[2], ~cdm_8_mark5_1_p4[3], cdm_8_mark5_1_p4[4], cdm_8_mark5_1_p4[5], cdm_8_mark5_1_p4[6], cdm_8_mark5_1_p4[7], cdm_8_mark5_1_p3, cdm_8_mark5_1_p2);  // AND_Gate
  assign controlled_buffer_3_out = and_4_out ? controlled_buffer_1_out : 8'bz;  // Controlled_Buffer controlled_buffer_3
  and and_4 (and_4_out, and_1_out, ~cdm_8_mark5_1_p3, cdm_8_mark5_1_p2, ~BallX[7]);  // AND_Gate
  assign controlled_buffer_1_out = and_5_out ? BallX : 8'bz;  // Controlled_Buffer controlled_buffer_4
  and and_5 (and_5_out, and_1_out, cdm_8_mark5_1_p3, cdm_8_mark5_1_p2);
  assign controlled_buffer_1_out = and_2_out ? BallY : 8'bz;  // Controlled_Buffer controlled_buffer_5
  assign controlled_buffer_1_out = and_3_out ? vxy : 8'bz;  // Controlled_Buffer controlled_buffer_6
  Register register_1 (
    .D(controlled_buffer_3_out), .en(and_4_out), .Q({rightbat, register_1_q}), .clk(clock_1_out));  // open: clr
  // Probe on BallX
  // Probe on BallY
  not not_2 (not_2_out, cdm_8_mark5_1_p2);
  ROM rom_1 (.addr(cdm_8_mark5_1_p4), .data(controlled_buffer_1_out), .sel(not_2_out));
  and and_6 (and_6_out, cdm_8_mark5_1_p2, ~and_5_out, ~and_2_out, ~and_3_out);  // AND_Gate
  RAM ram_1 (
    .addr(cdm_8_mark5_1_p4), .data(controlled_buffer_1_out), .sel(and_6_out), .clk(clock_1_out),
    .ld(cdm_8_mark5_1_p3));  // open: clr

  // Notes on the sheet:
  //   0xf3
  //   0xf4
  //   0xf5
  //   contents of rom_1 (hex, n*v repeats v):
  //   30 d0 f5 b0 d1 7 41 0 90 0 90 0 90 d2 7 48 d2 f3 ba d3 4 43 f e0 1f 84 d3 7 4c d3 1 74 e1 2e c3 d3
  //   e0 3e d3 f4 bf c3 d3 0 ee c3 c3 d3 f4 bf c3 d3 4 7c e1 72 c7 8f 8f 8f f 93 f 93 c c1 89 5 ed 4e 13
  //   e3 4b d1 ff 89 ee 43 1e e3 53 d1 ff d3 1f 1b e3 5a d1 ff 5 ea 68 d3 f4 bf d2 f3 ba d0 4 c5 ee 71 d3
  //   0 c5 c4 d0 0 c0 d0 3 c3 c1 d3 e0 3e 9 d3 1 43 f e1 8b 1a 2f d1 4 71 e1 89 35 1a 25 1f 17 ee 97 73 e1
  //   91 3f ee 97 3f 1a 2f 30 16 23 c4 d1 2 74 e1 a2 f 9b 92 ee c3 d1 3 74 e1 c3 d 8 94 25 94 25 12 27 94
  //   25 94 25 12 27 94 25 94 25 12 27 d0 55 12 d0 0 23 e 3f d c4 c7 f e0 cf 82 81 8e e3 cf 8d 12 e3 d3 8d
  //   5 ea dc 82 81 8e e3 dc 8d d0 1 41 5 e0 e3 82 d0 f3 a2 ee 0 d4 11*0 7 1a
endmodule

module Binaryto3Dig (
  input  [7:0] number,
  output [3:0] ones,
  output [3:0] tens,
  output [3:0] hundreds
);

  wire [11:0] bcdstep_1_bcdout, bcdstep_2_bcdout, bcdstep_3_bcdout, bcdstep_4_bcdout, bcdstep_5_bcdout,
       bcdstep_6_bcdout, bcdstep_7_bcdout;

  // Probe on number
  BCDstep bcdstep_1 (.BCD({12{1'b0}}), .BCDout(bcdstep_1_bcdout), .in(number[7]));
  BCDstep bcdstep_2 (.BCD(bcdstep_1_bcdout), .BCDout(bcdstep_2_bcdout), .in(number[6]));
  BCDstep bcdstep_3 (.BCD(bcdstep_4_bcdout), .BCDout(bcdstep_3_bcdout), .in(number[4]));
  BCDstep bcdstep_4 (.BCD(bcdstep_2_bcdout), .BCDout(bcdstep_4_bcdout), .in(number[5]));
  BCDstep bcdstep_5 (.BCD(bcdstep_3_bcdout), .BCDout(bcdstep_5_bcdout), .in(number[3]));
  BCDstep bcdstep_6 (.BCD(bcdstep_5_bcdout), .BCDout(bcdstep_6_bcdout), .in(number[2]));
  BCDstep bcdstep_7 (.BCD(bcdstep_6_bcdout), .BCDout(bcdstep_7_bcdout), .in(number[1]));
  BCDstep bcdstep_8 (.BCD(bcdstep_7_bcdout), .BCDout({hundreds, tens, ones}), .in(number[0]));
  // Probe on ones
  // Probe on tens
  // Probe on hundreds

  // Notes on the sheet:
  //   Double Dabble
  //   Do the number from binary to decimal
endmodule

module BCDstep (
  input  in,
  input  [11:0] BCD,
  output [11:0] BCDout
);

  wire and_1_out, and_2_out, and_3_out, and_4_out, and_5_out, and_6_out, or_1_out, or_2_out, or_3_out;
  wire [3:0] adder_1_out, adder_2_out, adder_3_out;
  wire [3:3] multiplexer_3_out;

  and and_1 (and_1_out, BCD[0], BCD[2]);
  or or_1 (or_1_out, and_1_out, BCD[3], and_2_out);
  and and_2 (and_2_out, BCD[2], BCD[1]);
  and and_3 (and_3_out, BCD[8], BCD[10]);
  or or_2 (or_2_out, and_3_out, BCD[11], and_4_out);
  and and_4 (and_4_out, BCD[10], BCD[9]);
  Adder #(.width(4)) adder_1 (.a(BCD[3:0]), .b(4'b0011), .out(adder_1_out));  // open: cin, cout
  and and_5 (and_5_out, BCD[4], BCD[6]);
  and and_6 (and_6_out, BCD[6], BCD[5]);
  Adder #(.width(4)) adder_2 (.a(BCD[7:4]), .b(4'b0011), .out(adder_2_out));  // open: cin, cout
  or or_3 (or_3_out, and_5_out, BCD[7], and_6_out);
  Adder #(.width(4)) adder_3 (.a(BCD[11:8]), .b(4'b0011), .out(adder_3_out));  // open: cin, cout
  Multiplexer #(.width(4), .enable("false")) multiplexer_1 (
    .in0(BCD[3:0]), .in1(adder_1_out), .out(BCDout[4:1]), .sel(or_1_out));
  Multiplexer #(.width(4), .enable("false")) multiplexer_2 (
    .in0(BCD[7:4]), .in1(adder_2_out), .out(BCDout[8:5]), .sel(or_3_out));
  Multiplexer #(.width(4), .enable("false")) multiplexer_3 (
    .in0(BCD[11:8]), .in1(adder_3_out), .out({multiplexer_3_out[3], BCDout[11:9]}), .sel(or_2_out));

  assign BCDout[0] = in;

  // Notes on the sheet:
  //   If the numbers are less than 5, add 3
  //   Shifts all bits by 1 and pushes in a new bit
endmodule

module CorrectJoystik (
  input  [4:0] Joystik,
  output [4:0] JoystikOut
);

  wire and_1_out, or_1_out;
  wire [4:0] not_1_out;

  assign not_1_out = ~Joystik;  // NOT_Gate not_1, 5 bits wide
  or or_1 (or_1_out, not_1_out[0], not_1_out[1], not_1_out[2]);
  and and_1 (and_1_out, or_1_out, not_1_out[3], not_1_out[4]);
  Multiplexer #(.width(5), .enable("false")) multiplexer_1 (
    .in0(not_1_out), .in1(5'b11101), .out(JoystikOut), .sel(and_1_out));

  // Notes on the sheet:
  //   Correct joystick
endmodule

module Diffusion (
  input  clock,
  input  mode,
  input  [2:0] Speed,
  output [2:0] SpeedOut
);

  wire comparator_1_eq, equal3bits_1_result, or_1_out, xor_1_out;
  wire [1:0] multiplexer_1_out, random_1_out;
  wire [2:0] adder_1_out, bit_extender_1_out, multiplexer_2_out;

  Random #(.width(2), .seed(12301029)) random_1 (.clk(clock), .out(random_1_out));  // open: next, clr
  Comparator #(.width(2)) comparator_1 (.a(random_1_out), .b(2'b10), .eq(comparator_1_eq));  // open: gt, lt
  assign bit_extender_1_out = {{1{multiplexer_1_out[1]}}, multiplexer_1_out};  // Bit_Extender bit_extender_1
  Multiplexer #(.width(2), .enable("false")) multiplexer_1 (
    .in0(random_1_out), .in1(2'b01), .out(multiplexer_1_out), .sel(comparator_1_eq));
  Multiplexer #(.width(3), .enable("false")) multiplexer_2 (
    .in0(bit_extender_1_out), .in1(3'b000), .out(multiplexer_2_out), .sel(mode));
  Adder #(.width(3)) adder_1 (.a(multiplexer_2_out), .b(Speed), .out(adder_1_out));  // open: cin, cout
  xor xor_1 (xor_1_out, Speed[2], adder_1_out[2]);
  Multiplexer #(.width(3), .enable("false")) multiplexer_3 (
    .in0(adder_1_out), .in1(Speed), .out(SpeedOut), .sel(or_1_out));
  or or_1 (or_1_out, xor_1_out, equal3bits_1_result);
  Equal3bits equal3bits_1 (.A(adder_1_out), .B(3'b000), .result(equal3bits_1_result));

  // Notes on the sheet:
  //   Diffusion of VY
endmodule

module CorrectRightBat (
  input  [4:0] RightBat,
  output [4:0] RightBatOut
);

  wire subtractor_1_bout;
  wire [4:0] subtractor_1_out;

  Subtractor #(.width(5)) subtractor_1 (
    .a(RightBat), .b(5'b00001), .out(subtractor_1_out), .bout(subtractor_1_bout));  // open: bin
  Multiplexer #(.width(5), .enable("false")) multiplexer_1 (
    .in0(subtractor_1_out), .in1(RightBat), .out(RightBatOut), .sel(subtractor_1_bout));

  // Notes on the sheet:
  //   Robot calculates the bottom pixel of the bat
  //   changes it to the middle pixel
endmodule

module Win_Mode (
  input  Mode,
  input  WinLeft,
  input  WinRight,
  output [6:0] _1,
  output [6:0] _2,
  output [6:0] _3,
  output [6:0] _4,
  output [6:0] _5,
  output [6:0] _6,
  output [6:0] _7,
  output [6:0] _8,
  output [6:0] _9,
  output [6:0] _10,
  output [6:0] _11,
  output [6:0] _12,
  output [6:0] _13,
  output [6:0] _14,
  output [6:0] _15,
  output [6:0] _16,
  output [6:0] _17,
  output [6:0] _18,
  output [6:0] _19,
  output [6:0] _20,
  output [6:0] _21,
  output [6:0] _22,
  output [6:0] _23,
  output [6:0] _24,
  output [6:0] _25,
  output [6:0] _26,
  output [6:0] _27,
  output [6:0] _28,
  output [6:0] _29,
  output [6:0] _30,
  output [6:0] _31,
  output [6:0] _32
);

  wire or_1_out;
  wire [1:0] des, multiplexer_21_out, multiplexer_26_out;

  Multiplexer #(.select(2), .width(7), .enable("false")) multiplexer_1 (
    .in0({7{1'b0}}), .in1({7{1'b0}}), .in2({7{1'b0}}), .in3({7{1'b0}}), .out(_1), .sel(des));
  Multiplexer #(.select(2), .width(7), .enable("false")) multiplexer_2 (
    .in0({7{1'b0}}), .in1(7'b0100100), .in2(7'b0100010), .in3({7{1'b0}}), .out(_9), .sel(des));
  Multiplexer #(.select(2), .width(7), .enable("false")) multiplexer_3 (
    .in0({7{1'b0}}), .in1(7'b0111110), .in2(7'b0111110), .in3(7'b0010100), .out(_17), .sel(des));
  Multiplexer #(.select(2), .width(7), .enable("false")) multiplexer_4 (
    .in0({7{1'b0}}), .in1(7'b0011110), .in2(7'b0111100), .in3({7{1'b0}}), .out(_25), .sel(des));
  Multiplexer #(.select(2), .width(7), .enable("false")) multiplexer_5 (
    .in0({7{1'b0}}), .in1(7'b0111110), .in2(7'b0111110), .in3(7'b0110100), .out(_2), .sel(des));
  Multiplexer #(.select(2), .width(7), .enable("false")) multiplexer_6 (
    .in0({7{1'b0}}), .in1(7'b0011000), .in2(7'b0011100), .in3({7{1'b0}}), .out(_10), .sel(des));
  Multiplexer #(.select(2), .width(7), .enable("false")) multiplexer_7 (
    .in0({7{1'b0}}), .in1(7'b0101010), .in2(7'b0101010), .in3(7'b0100010), .out(_18), .sel(des));
  Multiplexer #(.select(2), .width(7), .enable("false")) multiplexer_8 (
    .in0({7{1'b0}}), .in1({7{1'b0}}), .in2(7'b0000110), .in3({7{1'b0}}), .out(_26), .sel(des));
  Multiplexer #(.select(2), .width(7), .enable("false")) multiplexer_9 (
    .in0({7{1'b0}}), .in1(7'b0100000), .in2(7'b0100000), .in3(7'b0000010), .out(_3), .sel(des));
  Multiplexer #(.select(2), .width(7), .enable("false")) multiplexer_10 (
    .in0({7{1'b0}}), .in1({7{1'b0}}), .in2({7{1'b0}}), .in3(7'b0011100), .out(_11), .sel(des));
  Multiplexer #(.select(2), .width(7), .enable("false")) multiplexer_11 (
    .in0({7{1'b0}}), .in1(7'b0101010), .in2(7'b0101010), .in3(7'b0100010), .out(_19), .sel(des));
  Multiplexer #(.select(2), .width(7), .enable("false")) multiplexer_12 (
    .in0({7{1'b0}}), .in1(7'b0000010), .in2({7{1'b0}}), .in3(7'b0110100), .out(_27), .sel(des));
  Multiplexer #(.select(2), .width(7), .enable("false")) multiplexer_13 (
    .in0({7{1'b0}}), .in1(7'b0100000), .in2(7'b0100000), .in3(7'b0000010), .out(_4), .sel(des));
  Multiplexer #(.select(2), .width(7), .enable("false")) multiplexer_14 (
    .in0({7{1'b0}}), .in1(7'b0111110), .in2(7'b0111110), .in3(7'b0110100), .out(_5), .sel(des));
  Multiplexer #(.select(2), .width(7), .enable("false")) multiplexer_15 (
    .in0({7{1'b0}}), .in1(7'b0100010), .in2(7'b0101010), .in3(7'b0100010), .out(_13), .sel(des));
  Multiplexer #(.select(2), .width(7), .enable("false")) multiplexer_16 (
    .in0({7{1'b0}}), .in1(7'b0011100), .in2(7'b0111110), .in3(7'b0100010), .out(_12), .sel(des));
  Multiplexer #(.select(2), .width(7), .enable("false")) multiplexer_17 (
    .in0({7{1'b0}}), .in1(7'b0010100), .in2(7'b0100010), .in3(7'b0100010), .out(_20), .sel(des));
  Multiplexer #(.select(2), .width(7), .enable("false")) multiplexer_18 (
    .in0({7{1'b0}}), .in1({7{1'b0}}), .in2({7{1'b0}}), .in3(7'b0011100), .out(_21), .sel(des));
  Multiplexer #(.select(2), .width(7), .enable("false")) multiplexer_19 (
    .in0({7{1'b0}}), .in1(7'b0011100), .in2(7'b0011110), .in3(7'b0000010), .out(_28), .sel(des));
  Multiplexer #(.select(2), .width(7), .enable("false")) multiplexer_20 (
    .in0({7{1'b0}}), .in1(7'b0100000), .in2(7'b0100100), .in3(7'b0000010), .out(_29), .sel(des));
  Multiplexer #(.width(2)) multiplexer_21 (
    .in0(2'b01), .in1(2'b10), .out(multiplexer_21_out), .sel(WinLeft));  // open: en
  or or_1 (or_1_out, WinLeft, WinRight);
  Multiplexer #(.select(2), .width(7), .enable("false")) multiplexer_22 (
    .in0({7{1'b0}}), .in1({7{1'b0}}), .in2({7{1'b0}}), .in3({7{1'b0}}), .out(_6), .sel(des));
  Multiplexer #(.select(2), .width(7), .enable("false")) multiplexer_23 (
    .in0({7{1'b0}}), .in1(7'b0100010), .in2(7'b0101010), .in3(7'b0100010), .out(_14), .sel(des));
  Multiplexer #(.select(2), .width(7), .enable("false")) multiplexer_24 (
    .in0({7{1'b0}}), .in1(7'b0011110), .in2(7'b0000110), .in3({7{1'b0}}), .out(_22), .sel(des));
  Multiplexer #(.select(2), .width(7), .enable("false")) multiplexer_25 (
    .in0({7{1'b0}}), .in1(7'b0111110), .in2(7'b0100100), .in3(7'b0110100), .out(_30), .sel(des));
  Multiplexer #(.width(2)) multiplexer_26 (
    .in0(2'b00), .in1(multiplexer_21_out), .out(multiplexer_26_out), .sel(or_1_out));  // open: en
  Multiplexer #(.width(2)) multiplexer_27 (.in0(multiplexer_26_out), .in1(2'b11), .out(des), .sel(Mode));  // open: en
  Multiplexer #(.select(2), .width(7), .enable("false")) multiplexer_28 (
    .in0({7{1'b0}}), .in1(7'b0111110), .in2(7'b0011100), .in3({7{1'b0}}), .out(_7), .sel(des));
  Multiplexer #(.select(2), .width(7), .enable("false")) multiplexer_29 (
    .in0({7{1'b0}}), .in1(7'b0011100), .in2(7'b0000100), .in3(7'b0010100), .out(_15), .sel(des));
  Multiplexer #(.select(2), .width(7), .enable("false")) multiplexer_30 (
    .in0({7{1'b0}}), .in1(7'b0100100), .in2(7'b0011100), .in3({7{1'b0}}), .out(_23), .sel(des));
  Multiplexer #(.select(2), .width(7), .enable("false")) multiplexer_31 (
    .in0({7{1'b0}}), .in1({7{1'b0}}), .in2(7'b0011110), .in3({7{1'b0}}), .out(_31), .sel(des));
  Multiplexer #(.select(2), .width(7), .enable("false")) multiplexer_32 (
    .in0({7{1'b0}}), .in1(7'b0100100), .in2(7'b0100010), .in3({7{1'b0}}), .out(_8), .sel(des));
  Multiplexer #(.select(2), .width(7), .enable("false")) multiplexer_33 (
    .in0({7{1'b0}}), .in1({7{1'b0}}), .in2({7{1'b0}}), .in3(7'b0001000), .out(_16), .sel(des));
  Multiplexer #(.select(2), .width(7), .enable("false")) multiplexer_34 (
    .in0({7{1'b0}}), .in1(7'b0100100), .in2(7'b0100100), .in3({7{1'b0}}), .out(_24), .sel(des));
  Multiplexer #(.select(2), .width(7), .enable("false")) multiplexer_35 (
    .in0({7{1'b0}}), .in1({7{1'b0}}), .in2({7{1'b0}}), .in3({7{1'b0}}), .out(_32), .sel(des));

  // Notes on the sheet:
  //   Displaying the mode/result on the screen
  //   If mode 0:
  //   Not win - empty
  //   Winleft - ПОБЕДА
  //   Winright - ПРОВАЛ
  //   If mode 1, then infinity
  //   00
  //   10
  //   01
  //   11
endmodule

module Bats (
  input  [4:0] LeftbarY,
  input  clock,
  input  [4:0] RightbarY,
  output [4:0] LeftbarYOut,
  output plusleft,
  output minusleft,
  output [4:0] RightbarYOut,
  output minusright,
  output plusright
);

  wire comparator_1_gt;
  wire [4:0] correctrightbat_1_rightbatout, inc5bits_1_x_1, inc5bits_2_x_1, multiplexer_1_out,
       multiplexer_2_out, multiplexer_3_out, multiplexer_4_out, multiplexer_5_out, subtractor_1_out,
       subtractor_2_out;

  Inc5bits inc5bits_1 (.X(LeftbarYOut), .X_1(inc5bits_1_x_1));  // open: Cout
  CorrectRightBat correctrightbat_1 (.RightBat(RightbarY), .RightBatOut(correctrightbat_1_rightbatout));
  Comparator #(.width(5), .mode("unsigned")) comparator_1 (
    .a(correctrightbat_1_rightbatout), .b(5'b11101), .gt(comparator_1_gt));  // open: eq, lt
  Multiplexer #(.width(5), .enable("false")) multiplexer_1 (
    .in0(LeftbarYOut), .in1(inc5bits_1_x_1), .out(multiplexer_1_out), .sel(plusleft));
  Comparator #(.width(5), .mode("unsigned")) comparator_2 (
    .a(LeftbarYOut), .b(LeftbarY), .gt(minusleft), .lt(plusleft));  // open: eq
  Inc5bits inc5bits_2 (.X(RightbarYOut), .X_1(inc5bits_2_x_1));  // open: Cout
  Multiplexer #(.width(5), .enable("false")) multiplexer_2 (
    .in0(correctrightbat_1_rightbatout), .in1(5'b11101), .out(multiplexer_2_out), .sel(comparator_1_gt));
  Subtractor #(.width(5)) subtractor_1 (.a(LeftbarYOut), .b(5'b00001), .out(subtractor_1_out));  // open: bin, bout
  Multiplexer #(.width(5), .enable("false")) multiplexer_3 (
    .in0(RightbarYOut), .in1(inc5bits_2_x_1), .out(multiplexer_3_out), .sel(plusright));
  Comparator #(.width(5), .mode("unsigned")) comparator_3 (
    .a(RightbarYOut), .b(multiplexer_2_out), .gt(minusright), .lt(plusright));  // open: eq
  Subtractor #(.width(5)) subtractor_2 (.a(RightbarYOut), .b(5'b00001), .out(subtractor_2_out));  // open: bin, bout
  Register #(.width(5)) register_1 (.D(multiplexer_4_out), .Q(LeftbarYOut), .clk(clock));  // open: en, clr
  Multiplexer #(.width(5), .enable("false")) multiplexer_4 (
    .in0(multiplexer_1_out), .in1(subtractor_1_out), .out(multiplexer_4_out), .sel(minusleft));
  // Probe on LeftbarYOut
  Multiplexer #(.width(5), .enable("false")) multiplexer_5 (
    .in0(multiplexer_3_out), .in1(subtractor_2_out), .out(multiplexer_5_out), .sel(minusright));
  Register #(.width(5)) register_2 (.D(multiplexer_5_out), .Q(RightbarYOut), .clk(clock));  // open: en, clr

  // Notes on the sheet:
  //   Left Bat
  //   Right Bat
  //   Smooth movements of bats with joystick correction
endmodule

module Score (
  input  wall,
  input  resscore,
  input  reset,
  input  mode,
  input  clock,
  output max,
  output [7:0] Score
);

  wire and_1_out, multiplexer_1_out;

  Counter counter_1 (.count(wall), .Q(Score), .clk(clock), .clr(multiplexer_1_out));  // open: load, D, carry
  Multiplexer #(.enable("false")) multiplexer_1 (.in0(resscore), .in1(reset), .out(multiplexer_1_out), .sel(mode));
  D_Flip_Flop d_ff_1 (.clk(clock), .D(and_1_out), .Q(max), .reset(reset));  // open: Qn, preset, en
  and and_1 (and_1_out, Score[0], Score[1], Score[2], Score[3], ~Score[4], ~Score[5], ~Score[6], ~Score[7]);  // AND_Gate

  // Notes on the sheet:
  //   If mode is 0 score can be up to 15
endmodule

module Inc5bits (
  input  [4:0] X,
  output Cout,
  output [4:0] X_1
);

  wire [3:0] and_1_out;

  assign {Cout, and_1_out} = {and_1_out, 1'b1} & X;  // AND_Gate and_1, 5 bits wide
  assign X_1 = X ^ {and_1_out, 1'b1};  // XOR_Gate xor_1, 5 bits wide

  // Notes on the sheet:
  //   Return X + 1 for 5 bits number
endmodule

module Equal8Bits (
  input  [7:0] A,
  input  [7:0] B,
  output result
);

  wire [7:0] xnor_1_out;

  assign xnor_1_out = ~(A ^ B);  // XNOR_Gate xnor_1, 8 bits wide
  and and_1 (result, xnor_1_out[0], xnor_1_out[1], xnor_1_out[2], xnor_1_out[3], xnor_1_out[4], xnor_1_out[5], xnor_1_out[6], xnor_1_out[7]);

  // Notes on the sheet:
  //   if (A==B) return 1;
  //   else return 0;
endmodule

module Equal5Bits (
  input  [4:0] A,
  input  [4:0] B,
  output result
);

  wire [4:0] xnor_1_out;

  assign xnor_1_out = ~(A ^ B);  // XNOR_Gate xnor_1, 5 bits wide
  and and_1 (result, xnor_1_out[0], xnor_1_out[1], xnor_1_out[2], xnor_1_out[3], xnor_1_out[4]);

  // Notes on the sheet:
  //   if (A==B) return 1;
  //   else return 0;
endmodule

module Equal3bits (
  input  [2:0] A,
  input  [2:0] B,
  output result
);

  wire [2:0] xnor_1_out;

  assign xnor_1_out = ~(A ^ B);  // XNOR_Gate xnor_1, 3 bits wide
  and and_1 (result, xnor_1_out[0], xnor_1_out[1], xnor_1_out[2]);

  // Notes on the sheet:
  //   if (A==B) return 1;
  //   else return 0;
endmodule

module BatReflectVy (
  input  [2:0] Speed,
  input  up,
  input  down,
  output [2:0] SpeedOut
);

  wire comparator_1_eq, or_1_out, xor_1_out;
  wire [2:0] adder_1_out, multiplexer_1_out, multiplexer_2_out, subtractor_1_out;

  Adder #(.width(3)) adder_1 (.a(Speed), .b(3'b001), .out(adder_1_out));  // open: cin, cout
  Subtractor #(.width(3)) subtractor_1 (.a(Speed), .b(3'b001), .out(subtractor_1_out));  // open: bin, bout
  Multiplexer #(.width(3), .enable("false")) multiplexer_1 (
    .in0(Speed), .in1(adder_1_out), .out(multiplexer_1_out), .sel(up));
  xor xor_1 (xor_1_out, Speed[2], multiplexer_2_out[2]);
  Multiplexer #(.width(3), .enable("false")) multiplexer_2 (
    .in0(multiplexer_1_out), .in1(subtractor_1_out), .out(multiplexer_2_out), .sel(down));
  Multiplexer #(.width(3), .enable("false")) multiplexer_3 (
    .in0(multiplexer_2_out), .in1(Speed), .out(SpeedOut), .sel(or_1_out));
  or or_1 (or_1_out, xor_1_out, comparator_1_eq);
  Comparator #(.width(3)) comparator_1 (.a(multiplexer_2_out), .b(3'b000), .eq(comparator_1_eq));  // open: gt, lt

  // Notes on the sheet:
  //   If the ball hits the top pixel of the racket, its speed increases by 1
  //   If hots the bottmon pixel, its speed decreases by 1
endmodule
